// Logisim project flip_flop_homework_vug_sen_23_9908.circ as structural Verilog: 1 circuit, main circuit main
module main (
  input  in_1,
  input  in_2,
  input  in_3,
  input  in_4,
  input  in_5,
  input  in_6,
  input  in_7,
  input  in_8,
  input  in_9,
  input  in_10,
  input  in_11,
  input  in_12,
  input  in_13,
  input  in_14,
  input  in_15,
  input  in_16,
  input  in_17,
  input  in_18,
  input  in_19,
  input  in_20,
  output out_21,
  output out_22,
  output out_23,
  output out_24,
  output out_25,
  output out_26,
  output out_27,
  output out_28,
  output out_29,
  output out_30,
  output out_31,
  output out_32,
  output out_33,
  output out_34,
  output out_35,
  output out_36,
  output out_37,
  output out_38,
  output out_39,
  output out_40,
  output out_41,
  output out_42,
  output out_43,
  output out_44
);

  wire clock_1_out, clock_2_out, nand_1_out, nand_2_out, nand_3_out, nand_4_out, nand_5_out, nand_6_out,
       nand_7_out, nand_8_out, not_1_out, not_2_out, not_3_out, not_4_out;

  Clock clock_1 (.out(clock_1_out));
  S_R_Flip_Flop s_r_ff_1 (.S(in_1), .clk(clock_1_out), .R(in_9), .Q(out_21), .Qn(out_27));  // open: preset, reset, en
  S_R_Flip_Flop s_r_ff_2 (.S(in_4), .clk(clock_1_out), .R(in_12), .Q(out_24), .Qn(out_32));  // open: preset, reset, en
  S_R_Flip_Flop s_r_ff_3 (.S(in_5), .clk(clock_1_out), .R(in_13), .Q(out_25), .Qn(out_33));  // open: preset, reset, en
  not not_1 (not_1_out, in_17);
  Clock clock_2 (.out(clock_2_out));
  not not_2 (not_2_out, in_18);
  not not_3 (not_3_out, in_19);
  not not_4 (not_4_out, in_20);
  S_R_Flip_Flop s_r_ff_4 (.S(in_2), .clk(clock_1_out), .R(in_10), .Q(out_22), .Qn(out_28));  // open: preset, reset, en
  nand nand_1 (nand_1_out, in_17, clock_2_out);
  nand nand_2 (nand_2_out, not_1_out, clock_2_out);
  nand nand_3 (nand_3_out, in_18, clock_2_out);
  nand nand_4 (nand_4_out, not_2_out, clock_2_out);
  nand nand_5 (nand_5_out, in_19, clock_2_out);
  nand nand_6 (nand_6_out, not_3_out, clock_2_out);
  nand nand_7 (nand_7_out, in_20, clock_2_out);
  nand nand_8 (nand_8_out, not_4_out, clock_2_out);
  S_R_Flip_Flop s_r_ff_5 (.S(in_3), .clk(clock_1_out), .R(in_11), .Q(out_23), .Qn(out_29));  // open: preset, reset, en
  nand nand_9 (out_37, nand_1_out, out_38);
  nand nand_10 (out_38, out_37, nand_2_out);
  nand nand_11 (out_39, nand_3_out, out_40);
  nand nand_12 (out_40, out_39, nand_4_out);
  nand nand_13 (out_41, nand_5_out, out_42);
  nand nand_14 (out_42, out_41, nand_6_out);
  nand nand_15 (out_43, nand_7_out, out_44);
  nand nand_16 (out_44, out_43, nand_8_out);
  S_R_Flip_Flop s_r_ff_6 (.S(in_6), .clk(clock_1_out), .R(in_14), .Q(out_26), .Qn(out_34));  // open: preset, reset, en
  S_R_Flip_Flop s_r_ff_7 (.S(in_7), .clk(clock_1_out), .R(in_15), .Q(out_30), .Qn(out_35));  // open: preset, reset, en
  S_R_Flip_Flop s_r_ff_8 (.S(in_8), .clk(clock_1_out), .R(in_16), .Q(out_31), .Qn(out_36));  // open: preset, reset, en

  // Notes on the sheet:
  //   8-bit s_r flip flop
endmodule
